# Fritzing sketch Flame_Sensor (saved by Fritzing 0.9.3b)
breadboards: 1

parts:
  Raspberry_Pi_1 = Raspberry Pi 3 [part_number=RPI-3-V1.2]
  LED1 = Photodiode 5mm Black [package="5 mm [THT]"]
  R1 = Resistor [tolerance=±5% resistance=220 package="1206 [SMD]"]
  buz1 = Piezo Buzzer

nets:
  N1: Raspberry_Pi_1.GPIO4, buz1.pin_2
  N2: Raspberry_Pi_1.GND, R1.Pin_0, buz1.pin_1
  N3: Raspberry_Pi_1.GPIO21, LED1.cathode, R1.Pin_1
  N4: Raspberry_Pi_1.5V, LED1.anode

notes:
  GIPO 21 en bleu et Ground
  GIPO 4 en vert et Ground
  Rouge 5V
  Flame Sensor
  Passive Buzzer

custom parts:
  Photodiode 5mm Black: Photodiode 5mm Black/ Transparent
  Piezo Buzzer: Part from https://www.nutsvolts.com/magazine/article/november2012_SmileysWorkshop modified to be .3 in spacing to match the adafruit buzzer 5V breadboard friendly part.
